// Logisim project cpu3.circ as structural Verilog
module main (
);

  wire clock_1_out, cpu_1_io_trig, io_terminal_1_clock, io_terminal_1_io_wake, keyboard_1_avail, Reset_out,
       Resume_out, Stop_out;
  wire [6:0] keyboard_1_data;
  wire [14:0] cpu_1_romaddr;
  wire [15:0] cpu_1_io_out, io_terminal_1_io_in, rom_1_data;

  ROM #(.addrWidth(15), .dataWidth(16)) rom_1 (.addr(cpu_1_romaddr), .data(rom_1_data));
  CPU cpu_1 (
    .IO_TRIG(cpu_1_io_trig), .IO_OUT(cpu_1_io_out), .ROMAddr(cpu_1_romaddr), .IO_IN(io_terminal_1_io_in),
    .Reset(Reset_out), .Stop(Stop_out), .Resume(Resume_out), .ROMVal(rom_1_data),
    .IO_WAKE(io_terminal_1_io_wake), .Clk(clock_1_out));  // open: IO_CPUHLT, State, IO_SLEEP
  Button Reset (.out(Reset_out));
  Button Stop (.out(Stop_out));
  Button Resume (.out(Resume_out));
  Clock clock_1 (.out(clock_1_out));
  IO_TERMINAL io_terminal_1 (
    .IO_WAKE(io_terminal_1_io_wake), .IO_IN(io_terminal_1_io_in), .Clock(io_terminal_1_clock),
    .IO_TRIG(cpu_1_io_trig), .IO_OUT(cpu_1_io_out), .Avaliable(keyboard_1_avail), .KBVal(keyboard_1_data));
  Keyboard keyboard_1 (.clk(io_terminal_1_clock), .avail(keyboard_1_avail), .data(keyboard_1_data));  // open: re, clr

  // Notes on the sheet:
  //   contents of rom_1 (hex, n*v repeats v):
  //   9 eeee 81 69 7 e3 2 82 81 69 5 6f 69 27 72 69 14 70 2 2 9 6f 29 6b 18 16 38 16 9 6969 25 45 65 2 9
  //   21 10 2 2 9 66 29 61 18 16 38 16 9 69 29 6c 18 16 38 16 7 29 0 46 66 2 9 3c 10 2
endmodule

module CPU (
  input  Reset,
  input  Stop,
  input  Clk,
  input  Resume,
  input  IO_SLEEP,
  input  IO_WAKE,
  input  [15:0] IO_IN,
  input  [15:0] ROMVal,
  output IO_TRIG,
  output State,
  output [15:0] IO_OUT,
  output IO_CPUHLT,
  output [14:0] ROMAddr
);

  wire alu_1_carry, alu_1_zero, and_1_out, and_2_out, and_3_out, and_4_out, and_5_out, and_6_out, and_7_out,
       and_8_out, and_9_out, and_10_out, and_11_out, and_12_out, and_13_out, and_14_out, and_15_out,
       and_16_out, and_17_out, and_18_out, and_19_out, and_20_out, and_21_out, and_22_out, and_23_out,
       and_24_out, and_25_out, and_26_out, and_28_out, and_29_out, and_30_out, and_31_out, and_32_out,
       and_33_out, and_34_out, and_35_out, and_36_out, and_37_out, and_38_out, and_39_out, and_40_out,
       buffer_1_out, buffer_2_out, buffer_3_out, buffer_4_out, buffer_5_out, buffer_7_out, buffer_8_out,
       buffer_9_out, buffer_10_out, buffer_11_out, buffer_12_out, buffer_13_out, buffer_14_out,
       buffer_15_out, buffer_16_out, buffer_17_out, buffer_18_out, buffer_19_out, buffer_20_out,
       buffer_21_out, buffer_22_out, buffer_23_out, buffer_24_out, buffer_25_out, buffer_26_out,
       buffer_27_out, buffer_28_out, buffer_29_out, buffer_30_out, buffer_31_out, buffer_32_out,
       buffer_33_out, buffer_34_out, buffer_35_out, buffer_36_out, buffer_37_out, buffer_38_out,
       buffer_39_out, buffer_40_out, buffer_41_out, buffer_42_out, buffer_43_out, buffer_44_out,
       buffer_45_out, buffer_46_out, buffer_47_out, buffer_48_out, buffer_49_out, buffer_50_out,
       buffer_51_out, buffer_52_out, buffer_53_out, buffer_54_out, buffer_55_out, buffer_56_out,
       buffer_57_out, buffer_58_out, buffer_59_out, Carry_q, controlled_buffer_3_out,
       controlled_buffer_5_out, controlled_buffer_7_out, controlled_buffer_17_out, controlled_buffer_20_out,
       controlled_buffer_60_out, controlled_buffer_63_out, controlled_buffer_65_out, d_ff_1_q,
       demultiplexer_1_out0, demultiplexer_1_out1, demultiplexer_1_out2, demultiplexer_1_out3,
       demultiplexer_2_out0, demultiplexer_2_out1, demultiplexer_2_out2, demultiplexer_2_out4,
       demultiplexer_2_out9, demultiplexer_2_out10, demultiplexer_2_out11, demultiplexer_2_out12,
       demultiplexer_2_out13, demultiplexer_2_out14, demultiplexer_2_out15, demultiplexer_2_out16,
       demultiplexer_2_out17, demultiplexer_2_out18, demultiplexer_2_out19, demultiplexer_2_out20,
       demultiplexer_2_out21, demultiplexer_2_out22, demultiplexer_2_out23, demultiplexer_2_out24,
       demultiplexer_3_out0, demultiplexer_3_out1, demultiplexer_3_out2, demultiplexer_3_out3,
       demultiplexer_4_out0, demultiplexer_4_out1, demultiplexer_4_out2, demultiplexer_4_out3, or_1_out,
       or_2_out, or_3_out, or_4_out, or_6_out, or_7_out, or_8_out, or_9_out, or_10_out, or_11_out, or_12_out,
       or_13_out, or_14_out, priority_encoder_1_p1, priority_encoder_1_p2, priority_encoder_1_p4,
       priority_encoder_1_p5, pull_resistor_1_node, pull_resistor_2_node, pull_resistor_3_node,
       pull_resistor_4_node, pull_resistor_5_node, pull_resistor_6_node, pull_resistor_7_node,
       pull_resistor_10_node, rgbled_1_p1, risingedge_1_out_2, SP_carry, Zero_q;
  wire [1:0] buffer_6_out, priority_encoder_1_p3, priority_encoder_2_p3, STEP_q;
  wire [2:0] bit_extender_2_out, controlled_buffer_26_out;
  wire [7:0] bit_extender_1_out;
  wire [15:0] alu_1_sum, ALU_FRZ_q, controlled_buffer_2_out, controlled_buffer_6_out,
       controlled_buffer_18_out, controlled_buffer_19_out, controlled_buffer_22_out,
       controlled_buffer_23_out, controlled_buffer_29_out, controlled_buffer_62_out,
       controlled_buffer_64_out, controlled_buffer_66_out, INSTR_q, mmu_1_out_6, multiplexer_1_out,
       multiplexer_2_out, PC_q, REG_A_q, REG_B_q, REG_C_q, REG_D_q, register_2_q, SP_q;

  or or_1 (or_1_out, and_26_out, IO_SLEEP);
  and and_1 (and_1_out, ~d_ff_1_q, or_1_out);  // AND_Gate
  Pull_Resistor pull_resistor_1 (.node(pull_resistor_1_node));
  assign pull_resistor_1_node = Reset ? Reset : 1'bz;  // Controlled_Buffer controlled_buffer_1
  or or_2 (or_2_out, Stop, and_1_out);
  D_Flip_Flop #(.trigger("falling")) IS_HALT (.Q(IO_CPUHLT), .preset(and_1_out), .reset(or_3_out));  // open: D, clk, Qn
  or or_3 (or_3_out, and_2_out, Resume, pull_resistor_1_node);
  D_Flip_Flop d_ff_1 (.D(and_5_out), .clk(and_5_out), .Q(d_ff_1_q), .Qn(State), .preset(or_2_out), .reset(or_4_out));
  or or_4 (or_4_out, Resume, and_2_out, pull_resistor_1_node);
  and and_2 (and_2_out, IO_CPUHLT, d_ff_1_q, IO_WAKE);
  LED HLTLED (.in(IO_CPUHLT));
  Demultiplexer #(.select(2)) demultiplexer_1 (
    .out0(demultiplexer_1_out0), .out1(demultiplexer_1_out1), .out2(demultiplexer_1_out2),
    .out3(demultiplexer_1_out3), .in(and_3_out), .sel(STEP_q));
  Counter #(.max('h2), .trigger("falling"), .width(2)) STEP (
    .Q(STEP_q), .clk(buffer_1_out), .clr(controlled_buffer_5_out));  // open: load, D, count, carry, up
  buf buffer_1 (buffer_1_out, and_3_out);
  and and_3 (and_3_out, ~d_ff_1_q, Clk);  // AND_Gate
  LED led_1 (.in(State));
  // RGBLED rgbled_1: pin names not known; wires that end beside it: rgbled_1_p1, demultiplexer_1_out0
  or or_5 (rgbled_1_p1, demultiplexer_1_out1, demultiplexer_1_out2);
  // NoConnect on demultiplexer_1_out3
  buf buffer_2 (buffer_2_out, buffer_3_out);
  buf buffer_3 (buffer_3_out, buffer_4_out);
  buf buffer_4 (buffer_4_out, buffer_5_out);
  buf buffer_5 (buffer_5_out, pull_resistor_2_node);
  Pull_Resistor pull_resistor_2 (.node(pull_resistor_2_node));
  assign controlled_buffer_2_out = demultiplexer_1_out0 ? PC_q : 16'bz;  // Controlled_Buffer controlled_buffer_2
  Counter #(.max('hffff), .trigger("falling"), .width(16)) PC (
    .load(buffer_2_out), .D(controlled_buffer_29_out), .Q(PC_q), .clk(or_6_out), .clr(pull_resistor_1_node));  // open: count, carry, up
  or or_6 (or_6_out, demultiplexer_1_out0, or_7_out);
  or or_7 (or_7_out, pull_resistor_2_node, pull_resistor_3_node);
  Pull_Resistor pull_resistor_3 (.node(pull_resistor_3_node));
  Register #(.trigger("falling"), .width(16)) INSTR (
    .D(mmu_1_out_6), .Q(INSTR_q), .clk(demultiplexer_1_out0));  // open: en, clr
  assign controlled_buffer_3_out = demultiplexer_1_out0 ? demultiplexer_1_out0 : 1'bz;  // Controlled_Buffer controlled_buffer_3
  Pull_Resistor pull_resistor_4 (.node(pull_resistor_4_node));
  Pull_Resistor pull_resistor_5 (.node(pull_resistor_5_node));
  Pull_Resistor pull_resistor_6 (.node(pull_resistor_6_node));
  Pull_Resistor pull_resistor_7 (.node(pull_resistor_7_node));
  Bit_Extender #(.in_width(16), .out_width(8), .\type ("zero")) bit_extender_1 (.in(INSTR_q), .out(bit_extender_1_out));
  assign buffer_6_out = bit_extender_1_out[6:5];  // Buffer buffer_6, 2 bits wide
  assign pull_resistor_1_node = and_4_out ? and_4_out : 1'bz;  // Controlled_Buffer controlled_buffer_4
  and and_4 (and_4_out, demultiplexer_2_out1, demultiplexer_1_out1);
  and and_5 (and_5_out, demultiplexer_2_out2, demultiplexer_1_out1);
  and and_6 (and_6_out, demultiplexer_1_out1, or_9_out);
  assign controlled_buffer_5_out = and_7_out ? and_7_out : 1'bz;  // Controlled_Buffer controlled_buffer_5
  and and_7 (and_7_out, or_9_out, demultiplexer_1_out2);
  Multiplexer #(.select(2), .width(16)) multiplexer_1 (
    .in0(REG_A_q), .in1(REG_B_q), .in2(REG_C_q), .in3(REG_D_q), .out(multiplexer_1_out),
    .sel(priority_encoder_1_p3));
  assign controlled_buffer_6_out = and_6_out ? multiplexer_1_out : 16'bz;  // Controlled_Buffer controlled_buffer_6
  buf buffer_7 (buffer_7_out, and_6_out);
  buf buffer_8 (buffer_8_out, buffer_7_out);
  assign controlled_buffer_7_out = and_6_out ? buffer_8_out : 1'bz;  // Controlled_Buffer controlled_buffer_7
  or or_8 (or_8_out, demultiplexer_3_out0, demultiplexer_2_out0);
  assign controlled_buffer_5_out = or_8_out ? or_8_out : 1'bz;  // Controlled_Buffer controlled_buffer_8
  or or_9 (or_9_out, priority_encoder_1_p1, priority_encoder_1_p2, priority_encoder_1_p4, priority_encoder_1_p5);
  buf buffer_9 (buffer_9_out, and_11_out);
  buf buffer_10 (buffer_10_out, buffer_9_out);
  buf buffer_11 (buffer_11_out, buffer_10_out);
  buf buffer_12 (buffer_12_out, buffer_11_out);
  assign controlled_buffer_3_out = and_11_out ? buffer_12_out : 1'bz;  // Controlled_Buffer controlled_buffer_9
  // Priority_Encoder #(.select(2)) priority_encoder_1: pin names not known; wires that end beside it: priority_encoder_1_p1, priority_encoder_1_p2, priority_encoder_1_p3, priority_encoder_1_p4, priority_encoder_1_p5
  Pull_Resistor pull_resistor_8 (.node(priority_encoder_1_p3));
  assign controlled_buffer_2_out = and_11_out ? PC_q : 16'bz;  // Controlled_Buffer controlled_buffer_10
  assign controlled_buffer_6_out = and_9_out ? mmu_1_out_6 : 16'bz;  // Controlled_Buffer controlled_buffer_11
  buf buffer_13 (buffer_13_out, and_9_out);
  buf buffer_14 (buffer_14_out, buffer_13_out);
  assign controlled_buffer_7_out = and_9_out ? buffer_14_out : 1'bz;  // Controlled_Buffer controlled_buffer_12
  and and_8 (and_8_out, rgbled_1_p1, ~bit_extender_1_out[7]);  // AND_Gate
  Demultiplexer #(.select(5)) demultiplexer_2 (
    .out0(demultiplexer_2_out0), .out1(demultiplexer_2_out1), .out2(demultiplexer_2_out2),
    .out4(demultiplexer_2_out4), .out5(priority_encoder_1_p1), .out6(priority_encoder_1_p2),
    .out7(priority_encoder_1_p4), .out8(priority_encoder_1_p5), .out9(demultiplexer_2_out9),
    .out10(demultiplexer_2_out10), .out11(demultiplexer_2_out11), .out12(demultiplexer_2_out12),
    .out13(demultiplexer_2_out13), .out14(demultiplexer_2_out14), .out15(demultiplexer_2_out15),
    .out16(demultiplexer_2_out16), .out17(demultiplexer_2_out17), .out18(demultiplexer_2_out18),
    .out19(demultiplexer_2_out19), .out20(demultiplexer_2_out20), .out21(demultiplexer_2_out21),
    .out22(demultiplexer_2_out22), .out23(demultiplexer_2_out23), .out24(demultiplexer_2_out24),
    .in(and_8_out), .sel(bit_extender_1_out[4:0]));  // open: out3, out25, out26, out27, out28, out29, out30, out31
  assign pull_resistor_3_node = and_9_out ? and_9_out : 1'bz;  // Controlled_Buffer controlled_buffer_13
  and and_9 (and_9_out, demultiplexer_2_out9, demultiplexer_1_out2);
  and and_10 (and_10_out, demultiplexer_1_out1, demultiplexer_2_out10);
  and and_11 (and_11_out, demultiplexer_2_out9, demultiplexer_1_out1);
  assign controlled_buffer_2_out = and_10_out ? multiplexer_2_out : 16'bz;  // Controlled_Buffer controlled_buffer_14
  and and_12 (and_12_out, demultiplexer_2_out10, demultiplexer_1_out2);
  and and_13 (and_13_out, demultiplexer_1_out1, demultiplexer_2_out11);
  assign controlled_buffer_5_out = and_14_out ? and_14_out : 1'bz;  // Controlled_Buffer controlled_buffer_15
  and and_14 (and_14_out, demultiplexer_2_out11, demultiplexer_1_out2);
  buf buffer_15 (buffer_15_out, and_10_out);
  buf buffer_16 (buffer_16_out, and_12_out);
  buf buffer_17 (buffer_17_out, buffer_15_out);
  buf buffer_18 (buffer_18_out, buffer_16_out);
  assign controlled_buffer_3_out = and_10_out ? buffer_17_out : 1'bz;  // Controlled_Buffer controlled_buffer_16
  assign controlled_buffer_17_out = and_12_out ? buffer_18_out : 1'bz;  // Controlled_Buffer controlled_buffer_17
  assign controlled_buffer_18_out = and_12_out ? mmu_1_out_6 : 16'bz;  // Controlled_Buffer controlled_buffer_18
  and and_15 (and_15_out, demultiplexer_1_out1, demultiplexer_2_out12);
  and and_16 (and_16_out, demultiplexer_1_out1, demultiplexer_2_out13);
  and and_17 (and_17_out, demultiplexer_1_out1, demultiplexer_2_out14);
  // Priority_Encoder #(.select(2)) priority_encoder_2: pin names not known; wires that end beside it: and_15_out, and_16_out, priority_encoder_2_p3, and_17_out
  Pull_Resistor pull_resistor_9 (.node(priority_encoder_2_p3));
  buf buffer_19 (buffer_19_out, and_13_out);
  assign controlled_buffer_19_out = and_13_out ? REG_A_q : 16'bz;  // Controlled_Buffer controlled_buffer_19
  and and_18 (and_18_out, demultiplexer_1_out1, demultiplexer_2_out15);
  or or_10 (or_10_out, demultiplexer_2_out15, demultiplexer_2_out14, demultiplexer_2_out13, demultiplexer_2_out12);
  or or_11 (or_11_out, and_15_out, and_16_out, and_17_out, and_18_out);
  assign bit_extender_2_out = {{1{1'b0}}, priority_encoder_2_p3};  // Bit_Extender bit_extender_2
  buf buffer_20 (buffer_20_out, or_11_out);
  buf buffer_21 (buffer_21_out, buffer_19_out);
  assign controlled_buffer_20_out = and_13_out ? buffer_21_out : 1'bz;  // Controlled_Buffer controlled_buffer_20
  buf buffer_22 (buffer_22_out, buffer_20_out);
  assign controlled_buffer_2_out = and_13_out ? multiplexer_2_out : 16'bz;  // Controlled_Buffer controlled_buffer_21
  buf buffer_23 (buffer_23_out, buffer_22_out);
  and and_19 (and_19_out, demultiplexer_2_out16, demultiplexer_1_out1);
  and and_20 (and_20_out, demultiplexer_2_out17, Zero_q, demultiplexer_1_out1);
  and and_21 (and_21_out, demultiplexer_1_out2, or_10_out);
  assign controlled_buffer_22_out = buffer_23_out ? multiplexer_2_out : 16'bz;  // Controlled_Buffer controlled_buffer_22
  assign controlled_buffer_23_out = buffer_23_out ? REG_A_q : 16'bz;  // Controlled_Buffer controlled_buffer_23
  assign pull_resistor_4_node = or_11_out ? or_11_out : 1'bz;  // Controlled_Buffer controlled_buffer_24
  assign pull_resistor_5_node = or_11_out ? or_11_out : 1'bz;  // Controlled_Buffer controlled_buffer_25
  and and_22 (and_22_out, demultiplexer_2_out19, Carry_q, demultiplexer_1_out1);
  and and_23 (and_23_out, demultiplexer_2_out18, ~Zero_q, demultiplexer_1_out1);  // AND_Gate
  or or_12 (or_12_out, and_19_out, and_20_out, and_23_out, and_22_out, and_25_out);
  assign controlled_buffer_26_out = or_11_out ? bit_extender_2_out : 3'bz;  // Controlled_Buffer controlled_buffer_26
  buf buffer_24 (buffer_24_out, and_21_out);
  buf buffer_25 (buffer_25_out, buffer_24_out);
  assign controlled_buffer_18_out = and_21_out ? ALU_FRZ_q : 16'bz;  // Controlled_Buffer controlled_buffer_27
  assign controlled_buffer_17_out = buffer_25_out ? buffer_25_out : 1'bz;  // Controlled_Buffer controlled_buffer_28
  assign controlled_buffer_29_out = buffer_28_out ? multiplexer_2_out : 16'bz;  // Controlled_Buffer controlled_buffer_29
  assign pull_resistor_2_node = or_12_out ? or_12_out : 1'bz;  // Controlled_Buffer controlled_buffer_30
  or or_13 (or_13_out, demultiplexer_2_out20, demultiplexer_2_out19, demultiplexer_2_out18, demultiplexer_2_out17, demultiplexer_2_out16);
  and and_24 (and_24_out, or_13_out, demultiplexer_1_out2);
  assign controlled_buffer_5_out = and_24_out ? and_24_out : 1'bz;  // Controlled_Buffer controlled_buffer_31
  and and_25 (and_25_out, demultiplexer_2_out20, ~Carry_q, demultiplexer_1_out1);  // AND_Gate
  buf buffer_26 (buffer_26_out, or_12_out);
  buf buffer_27 (buffer_27_out, buffer_26_out);
  buf buffer_28 (buffer_28_out, buffer_27_out);
  and and_26 (and_26_out, demultiplexer_2_out21, demultiplexer_1_out1);
  and and_27 (IO_TRIG, demultiplexer_2_out22, demultiplexer_1_out1);
  buf buffer_29 (buffer_29_out, and_26_out);
  buf buffer_30 (buffer_30_out, buffer_29_out);
  buf buffer_31 (buffer_31_out, buffer_30_out);
  buf buffer_32 (buffer_32_out, buffer_31_out);
  assign controlled_buffer_5_out = and_26_out ? buffer_32_out : 1'bz;  // Controlled_Buffer controlled_buffer_32
  buf buffer_33 (buffer_33_out, and_29_out);
  Register #(.width(16)) register_1 (.D(multiplexer_2_out), .Q(IO_OUT), .clk(and_31_out));  // open: en, clr
  buf buffer_34 (buffer_34_out, buffer_33_out);
  buf buffer_35 (buffer_35_out, buffer_34_out);
  assign controlled_buffer_6_out = and_29_out ? IO_IN : 16'bz;  // Controlled_Buffer controlled_buffer_33
  assign controlled_buffer_7_out = and_29_out ? buffer_35_out : 1'bz;  // Controlled_Buffer controlled_buffer_34
  and and_28 (and_28_out, demultiplexer_2_out22, demultiplexer_1_out2);
  and and_29 (and_29_out, demultiplexer_1_out1, demultiplexer_2_out23);
  assign controlled_buffer_5_out = and_28_out ? and_28_out : 1'bz;  // Controlled_Buffer controlled_buffer_35
  Register #(.width(16)) register_2 (.D(multiplexer_2_out), .Q(register_2_q), .clk(and_32_out));  // open: en, clr
  assign controlled_buffer_5_out = and_30_out ? and_30_out : 1'bz;  // Controlled_Buffer controlled_buffer_36
  assign controlled_buffer_5_out = and_31_out ? buffer_36_out : 1'bz;  // Controlled_Buffer controlled_buffer_37
  and and_30 (and_30_out, demultiplexer_1_out2, demultiplexer_2_out23);
  and and_31 (and_31_out, demultiplexer_1_out1, demultiplexer_2_out24);
  buf buffer_36 (buffer_36_out, buffer_37_out);
  buf buffer_37 (buffer_37_out, buffer_38_out);
  buf buffer_38 (buffer_38_out, and_31_out);
  buf buffer_39 (buffer_39_out, and_32_out);
  buf buffer_40 (buffer_40_out, buffer_39_out);
  buf buffer_41 (buffer_41_out, buffer_40_out);
  assign controlled_buffer_6_out = buffer_41_out ? REG_A_q : 16'bz;  // Controlled_Buffer controlled_buffer_38
  and and_32 (and_32_out, demultiplexer_1_out1, demultiplexer_2_out4);
  and and_33 (and_33_out, demultiplexer_1_out2, demultiplexer_2_out4);
  buf buffer_42 (buffer_42_out, buffer_41_out);
  buf buffer_43 (buffer_43_out, buffer_42_out);
  assign controlled_buffer_7_out = buffer_41_out ? buffer_43_out : 1'bz;  // Controlled_Buffer controlled_buffer_39
  assign controlled_buffer_18_out = and_33_out ? register_2_q : 16'bz;  // Controlled_Buffer controlled_buffer_40
  buf buffer_44 (buffer_44_out, and_33_out);
  buf buffer_45 (buffer_45_out, buffer_44_out);
  buf buffer_46 (buffer_46_out, buffer_45_out);
  assign controlled_buffer_2_out = and_34_out ? SP_q : 16'bz;  // Controlled_Buffer controlled_buffer_41
  assign controlled_buffer_17_out = and_33_out ? buffer_46_out : 1'bz;  // Controlled_Buffer controlled_buffer_42
  and and_34 (and_34_out, demultiplexer_3_out1, demultiplexer_1_out2);
  and and_35 (and_35_out, demultiplexer_3_out1, demultiplexer_1_out1);
  assign pull_resistor_7_node = and_35_out ? and_35_out : 1'bz;  // Controlled_Buffer controlled_buffer_43
  buf buffer_47 (buffer_47_out, and_34_out);
  buf buffer_48 (buffer_48_out, buffer_47_out);
  buf buffer_49 (buffer_49_out, buffer_48_out);
  assign controlled_buffer_19_out = and_34_out ? multiplexer_2_out : 16'bz;  // Controlled_Buffer controlled_buffer_44
  assign controlled_buffer_20_out = and_34_out ? buffer_49_out : 1'bz;  // Controlled_Buffer controlled_buffer_45
  and and_36 (and_36_out, demultiplexer_3_out2, demultiplexer_1_out1);
  and and_37 (and_37_out, demultiplexer_3_out2, demultiplexer_1_out2);
  buf buffer_50 (buffer_50_out, and_36_out);
  buf buffer_51 (buffer_51_out, buffer_50_out);
  assign controlled_buffer_3_out = and_36_out ? buffer_51_out : 1'bz;  // Controlled_Buffer controlled_buffer_46
  assign controlled_buffer_2_out = and_36_out ? SP_q : 16'bz;  // Controlled_Buffer controlled_buffer_47
  and and_38 (and_38_out, demultiplexer_3_out3, demultiplexer_1_out1);
  and and_39 (and_39_out, demultiplexer_3_out3, demultiplexer_1_out2);
  buf buffer_52 (buffer_52_out, and_37_out);
  buf buffer_53 (buffer_53_out, buffer_52_out);
  Pull_Resistor pull_resistor_10 (.node(pull_resistor_10_node));
  assign pull_resistor_10_node = and_37_out ? buffer_53_out : 1'bz;  // Controlled_Buffer controlled_buffer_48
  assign controlled_buffer_6_out = and_37_out ? mmu_1_out_6 : 16'bz;  // Controlled_Buffer controlled_buffer_49
  assign controlled_buffer_7_out = pull_resistor_10_node ? pull_resistor_10_node : 1'bz;  // Controlled_Buffer controlled_buffer_50
  assign pull_resistor_6_node = pull_resistor_10_node ? pull_resistor_10_node : 1'bz;  // Controlled_Buffer controlled_buffer_51
  and and_40 (and_40_out, rgbled_1_p1, bit_extender_1_out[7]);
  Demultiplexer #(.select(5)) demultiplexer_3 (
    .out0(demultiplexer_3_out0), .out1(demultiplexer_3_out1), .out2(demultiplexer_3_out2),
    .out3(demultiplexer_3_out3), .in(and_40_out), .sel(bit_extender_1_out[4:0]));  // open: out4, out5, out6, out7, out8, out9, out10, out11, out12, out13, out14, out15, out16, out17, out18, out19, out20, out21, out22, out23, out24, out25, out26, out27, out28, out29, out30, out31
  buf buffer_54 (buffer_54_out, and_38_out);
  buf buffer_55 (buffer_55_out, buffer_54_out);
  buf buffer_56 (buffer_56_out, buffer_55_out);
  assign controlled_buffer_2_out = and_38_out ? SP_q : 16'bz;  // Controlled_Buffer controlled_buffer_52
  assign controlled_buffer_20_out = and_38_out ? buffer_56_out : 1'bz;  // Controlled_Buffer controlled_buffer_53
  buf buffer_57 (buffer_57_out, buffer_59_out);
  assign controlled_buffer_19_out = and_38_out ? PC_q : 16'bz;  // Controlled_Buffer controlled_buffer_54
  buf buffer_58 (buffer_58_out, buffer_57_out);
  assign pull_resistor_7_node = and_39_out ? and_39_out : 1'bz;  // Controlled_Buffer controlled_buffer_55
  buf buffer_59 (buffer_59_out, and_39_out);
  assign controlled_buffer_29_out = buffer_58_out ? multiplexer_2_out : 16'bz;  // Controlled_Buffer controlled_buffer_56
  assign pull_resistor_2_node = and_39_out ? and_39_out : 1'bz;  // Controlled_Buffer controlled_buffer_57
  Pull_Resistor pull_resistor_11 (.node(controlled_buffer_5_out));
  or or_14 (or_14_out, pull_resistor_6_node, pull_resistor_7_node);
  assign pull_resistor_7_node = risingedge_1_out_2 ? risingedge_1_out_2 : 1'bz;  // Controlled_Buffer controlled_buffer_58
  Pull_Resistor pull_resistor_12 (.node(controlled_buffer_3_out));
  Pull_Resistor pull_resistor_13 (.node(controlled_buffer_20_out));
  Pull_Resistor pull_resistor_14 (.node(controlled_buffer_7_out));
  Demultiplexer #(.select(2)) demultiplexer_4 (
    .out0(demultiplexer_4_out0), .out1(demultiplexer_4_out1), .out2(demultiplexer_4_out2),
    .out3(demultiplexer_4_out3), .in(controlled_buffer_7_out), .sel(buffer_6_out));
  Counter #(.max('hffff), .width(16)) SP (
    .Q(SP_q), .carry(SP_carry), .up(pull_resistor_6_node), .clk(or_14_out), .clr(pull_resistor_1_node));  // open: load, D, count
  RisingEdge risingedge_1 (.out_2(risingedge_1_out_2), .in_1(SP_carry));
  assign controlled_buffer_17_out = demultiplexer_4_out0 ? demultiplexer_4_out0 : 1'bz;  // Controlled_Buffer controlled_buffer_59
  assign controlled_buffer_60_out = demultiplexer_4_out3 ? demultiplexer_4_out3 : 1'bz;  // Controlled_Buffer controlled_buffer_60
  ALU alu_1 (
    .Sum(alu_1_sum), .Zero(alu_1_zero), .Carry(alu_1_carry), .A(controlled_buffer_23_out),
    .B(controlled_buffer_22_out), .Sel(controlled_buffer_26_out));
  D_Flip_Flop #(.trigger("falling")) Zero (
    .D(alu_1_zero), .clk(pull_resistor_4_node), .Q(Zero_q));  // open: Qn, preset, reset
  assign controlled_buffer_18_out = controlled_buffer_7_out ? controlled_buffer_6_out : 16'bz;  // Controlled_Buffer controlled_buffer_61
  assign controlled_buffer_62_out = controlled_buffer_7_out ? controlled_buffer_6_out : 16'bz;  // Controlled_Buffer controlled_buffer_62
  assign controlled_buffer_63_out = demultiplexer_4_out1 ? demultiplexer_4_out1 : 1'bz;  // Controlled_Buffer controlled_buffer_63
  assign controlled_buffer_64_out = controlled_buffer_7_out ? controlled_buffer_6_out : 16'bz;  // Controlled_Buffer controlled_buffer_64
  assign controlled_buffer_65_out = demultiplexer_4_out2 ? demultiplexer_4_out2 : 1'bz;  // Controlled_Buffer controlled_buffer_65
  assign controlled_buffer_66_out = controlled_buffer_7_out ? controlled_buffer_6_out : 16'bz;  // Controlled_Buffer controlled_buffer_66
  Pull_Resistor pull_resistor_15 (.node(alu_1_sum));
  D_Flip_Flop #(.trigger("falling")) Carry (
    .D(alu_1_carry), .clk(pull_resistor_4_node), .Q(Carry_q));  // open: Qn, preset, reset
  MMU mmu_1 (
    .ROMADDR(ROMAddr), .out_6(mmu_1_out_6), .ADDR(controlled_buffer_2_out), .RD(controlled_buffer_3_out),
    .WRT(controlled_buffer_20_out), .VAL(controlled_buffer_19_out), .ROMOUT(ROMVal));
  Pull_Resistor pull_resistor_16 (.node(controlled_buffer_18_out));
  Pull_Resistor pull_resistor_17 (.node(controlled_buffer_62_out));
  Pull_Resistor pull_resistor_18 (.node(controlled_buffer_64_out));
  Pull_Resistor pull_resistor_19 (.node(controlled_buffer_66_out));
  Pull_Resistor pull_resistor_20 (.node(controlled_buffer_17_out));
  Pull_Resistor pull_resistor_21 (.node(controlled_buffer_63_out));
  Pull_Resistor pull_resistor_22 (.node(controlled_buffer_65_out));
  Register #(.trigger("falling"), .width(16)) ALU_FRZ (
    .D(alu_1_sum), .Q(ALU_FRZ_q), .clk(pull_resistor_5_node));  // open: en, clr
  Register #(.width(16)) REG_A (
    .D(controlled_buffer_18_out), .Q(REG_A_q), .clk(controlled_buffer_17_out), .clr(pull_resistor_1_node));  // open: en
  Register #(.width(16)) REG_B (
    .D(controlled_buffer_62_out), .Q(REG_B_q), .clk(controlled_buffer_63_out), .clr(pull_resistor_1_node));  // open: en
  Register #(.width(16)) REG_C (
    .D(controlled_buffer_64_out), .Q(REG_C_q), .clk(controlled_buffer_65_out), .clr(pull_resistor_1_node));  // open: en
  Register #(.width(16)) REG_D (
    .D(controlled_buffer_66_out), .Q(REG_D_q), .clk(controlled_buffer_60_out), .clr(pull_resistor_1_node));  // open: en
  Pull_Resistor pull_resistor_23 (.node(controlled_buffer_60_out));
  Multiplexer #(.select(2), .width(16)) multiplexer_2 (
    .in0(REG_A_q), .in1(REG_B_q), .in2(REG_C_q), .in3(REG_D_q), .out(multiplexer_2_out), .sel(buffer_6_out));

  // Notes on the sheet:
  //   hacky >>>>
  //   i hate this part
  //   TICK
  //   RED-FETCH
  //   GRN - EXEC
  //   ADDR
  //   WRTVAL
  //   RD
  //   WR
  //   OUT
  //   WR_SEL_V
  //   WR_SEL
  //   SEL
  //   SEL_VAL
  //   A_VAL
  //   B_VAL
  //   C_VAL
  //   D_VAL
  //   WR_A_VAL
  //   WR_B_VAL
  //   WR_C_VAL
  //   WR_D_VAL
  //   WR_A
  //   WR_B
  //   WR_C
  //   WR_D
  //   ALU_A
  //   ALU_B
  //   ALU_Z
  //   ALU_C
  //   ALU_R
  //   ALU_S
  //   C_FLAG
  //   Z_FLAG
  //   FLAG
  //   FR_VAL
  //   FR
  //   SP
  //   SP_POP
  //   SP_PUSH
  //   skip pc
  //   t1/t2
  //   vv skip additional clocks
  //   LD R,R
  //   RST
  //   STOP
  //   LD R,V
  //   LD A,[R]
  //   LD [R],A
  //   ADD SUB MUL CMP
  //   JP
  //   Z
  //   C
  //   NZ
  //   NC
  //   Skp JP ^
  //   IOHALT >
  //   ior
  //   PUSH r
  //   POP r
  //   CALL r
  //   JUMP
  //   JADDR
  //   PC
  //   RST
endmodule

module MMU (
  input  [15:0] ROMOUT,
  input  [15:0] ADDR,
  input  [15:0] VAL,
  input  RD,
  input  WRT,
  output [15:0] out_6,
  output [14:0] ROMADDR
);

  wire and_1_out, and_2_out, and_3_out, buffer_2_out, buffer_3_out, not_1_out, or_1_out;
  wire [15:0] buffer_1_out, buffer_4_out, multiplexer_1_out, ram_1_dout, undriven;

  Register #(.trigger("high"), .width(15)) register_1 (
    .D(buffer_1_out[14:0]), .Q(ROMADDR), .clk(and_3_out));  // open: en, clr
  assign buffer_1_out = ADDR;  // Buffer buffer_1, 16 bits wide
  Pull_Resistor pull_resistor_1 (.node(ADDR));
  and and_1 (and_1_out, buffer_1_out[15], or_1_out);
  and and_2 (and_2_out, buffer_1_out[15], buffer_3_out);
  or or_1 (or_1_out, buffer_2_out, buffer_3_out);
  buf buffer_2 (buffer_2_out, RD);
  buf buffer_3 (buffer_3_out, WRT);
  Pull_Resistor pull_resistor_2 (.node(RD));
  Pull_Resistor pull_resistor_3 (.node(WRT));
  RAM #(.addrWidth(15), .dataWidth(16)) ram_1 (
    .addr(buffer_1_out[14:0]), .we(and_2_out), .oe(and_1_out), .clk(and_1_out), .din(buffer_4_out),
    .dout(ram_1_dout));
  and and_3 (and_3_out, ~buffer_1_out[15], or_1_out);  // AND_Gate
  assign buffer_4_out = VAL;  // Buffer buffer_4, 16 bits wide
  Pull_Resistor pull_resistor_4 (.node(VAL));
  ErrorPullDown16 errorpulldown16_1 (.in_1({undriven[15], ram_1_dout[15], undriven[14], ram_1_dout[14], undriven[13], ram_1_dout[13], undriven[12], ram_1_dout[12], undriven[11], ram_1_dout[11], undriven[10], ram_1_dout[10], undriven[9], ram_1_dout[9], undriven[8], ram_1_dout[8], undriven[7], ram_1_dout[7], undriven[6], ram_1_dout[6], undriven[5], ram_1_dout[5], undriven[4], ram_1_dout[4], undriven[3], ram_1_dout[3], undriven[2], ram_1_dout[2], undriven[1], ram_1_dout[1], undriven[0], ram_1_dout[0]}));
  Multiplexer #(.width(16)) multiplexer_1 (.in0(undriven), .in1(ROMOUT), .out(multiplexer_1_out), .sel(not_1_out));
  not not_1 (not_1_out, buffer_1_out[15]);
  Register #(.trigger("high"), .width(16)) register_2 (
    .D(multiplexer_1_out), .Q(out_6), .clk(or_1_out));  // open: en, clr
endmodule

module ALU (
  input  [15:0] A,
  input  [15:0] B,
  input  [2:0] Sel,
  output Carry,
  output [15:0] Sum,
  output Zero
);

  wire adder_1_cout, subtractor_1_bout;
  wire [1:0] comparator_1_lt;
  wire [15:0] adder_1_out, bit_extender_1_out, multiplier_1_out, subtractor_1_out;

  Adder #(.width(16)) adder_1 (.a(A), .b(B), .out(adder_1_out), .cout(adder_1_cout));  // open: cin
  Subtractor #(.width(16)) subtractor_1 (.a(A), .b(B), .out(subtractor_1_out), .bout(subtractor_1_bout));  // open: bin
  Multiplier #(.width(16)) multiplier_1 (.a(A), .b(B), .out(multiplier_1_out));  // open: cin, cout
  Comparator #(.mode("unsigned"), .width(16)) comparator_1 (
    .a(A), .b(B), .gt(comparator_1_lt[1]), .lt(comparator_1_lt[0]));  // open: eq
  assign bit_extender_1_out = {{14{1'b0}}, comparator_1_lt};  // Bit_Extender bit_extender_1
  Multiplexer #(.select(3), .width(16)) multiplexer_1 (
    .in0(adder_1_out), .in1(subtractor_1_out), .in2(multiplier_1_out), .in3(bit_extender_1_out), .out(Sum),
    .sel(Sel));  // open: in4, in5, in6, in7
  Pull_Resistor pull_resistor_1 (.node(Carry));
  Multiplexer #(.select(3)) multiplexer_2 (
    .in0(adder_1_cout), .in1(subtractor_1_bout), .in3(comparator_1_lt[1]), .out(Carry), .sel(Sel));  // open: in2, in4, in5, in6, in7
  Comparator #(.mode("unsigned"), .width(16)) comparator_2 (.a(Sum), .b({16{1'b0}}), .eq(Zero));  // open: gt, lt

  // Notes on the sheet:
  //   Carry: pull=down
endmodule

module IO_TERMINAL (
  input  IO_TRIG,
  input  [15:0] IO_OUT,
  input  [6:0] KBVal,
  input  Avaliable,
  output IO_WAKE,
  output [15:0] IO_IN,
  output Clock
);

  wire and_1_out, and_2_out, comparator_1_eq, comparator_2_eq, or_1_out;
  wire [6:0] bit_extender_1_out;

  Comparator #(.mode("unsigned"), .width(16)) comparator_1 (
    .a(16'hfffe), .b(IO_OUT), .eq(comparator_1_eq));  // open: gt, lt
  Comparator #(.mode("unsigned"), .width(16)) comparator_2 (
    .a({16{1'b1}}), .b(IO_OUT), .eq(comparator_2_eq));  // open: gt, lt
  or or_1 (or_1_out, comparator_1_eq, comparator_2_eq);
  and and_1 (and_1_out, ~or_1_out, IO_TRIG);  // AND_Gate
  Bit_Extender #(.in_width(16), .out_width(7), .\type ("zero")) bit_extender_1 (.in(IO_OUT), .out(bit_extender_1_out));
  and and_2 (and_2_out, comparator_1_eq, IO_TRIG);
  TTY tty_1 (.data(bit_extender_1_out), .clk(and_1_out), .clr(and_2_out));  // open: we
  assign IO_IN = {{9{1'b0}}, KBVal};  // Bit_Extender bit_extender_2

  assign Clock = IO_TRIG;
  assign IO_WAKE = Avaliable;
endmodule

module RisingEdge (
  input  in_1,
  output out_2
);

  wire not_1_out, not_2_out, not_3_out;

  not not_1 (not_1_out, in_1);
  and and_1 (out_2, in_1, not_2_out);
  not not_2 (not_2_out, not_3_out);
  not not_3 (not_3_out, not_1_out);
endmodule

module FallingEdge (
  input  in_1,
  output out_2
);

  wire buffer_1_out, not_1_out, not_2_out, not_3_out;

  buf buffer_1 (buffer_1_out, in_1);
  not not_1 (not_1_out, not_2_out);
  not not_2 (not_2_out, buffer_1_out);
  and and_1 (out_2, not_1_out, not_3_out);
  not not_3 (not_3_out, in_1);
endmodule

module ErrorPullDown16 (
  input  [15:0] in_1,
  output [15:0] out_2
);


  assign out_2 = in_1;

  // Notes on the sheet:
  //   out_2: pull=down
  //   in_1: pull=down
endmodule
